// Logisim project 02-decoder-display.circ as structural Verilog: 1 circuit, main circuit main
module main (
  input  in_1,
  input  [1:0] P3_4_P3_3,
  output display_3,
  output display_2,
  output display_1,
  output display_0
);

  Decoder #(.select(2)) decoder_1 (
    .out0(display_0), .out1(display_1), .out2(display_2), .out3(display_3), .sel(P3_4_P3_3), .en(in_1));
endmodule
