// Logisim project 02-display7.circ as structural Verilog: 1 circuit, main circuit main
module main (
  input  P1_0,
  input  P1_1,
  input  P1_2,
  input  P1_3,
  input  P1_4,
  input  P1_5,
  input  P1_6,
  input  P1_7
);

  wire not_1_out, not_2_out, not_3_out, not_4_out, not_5_out, not_6_out, not_7_out, not_8_out;

  not not_1 (not_1_out, P1_3);
  not not_2 (not_2_out, P1_0);
  not not_3 (not_3_out, P1_1);
  not not_4 (not_4_out, P1_2);
  _7_Segment_Display u_7_segment_display_1 (
    .g(not_7_out), .f(not_6_out), .a(not_2_out), .b(not_3_out), .e(not_5_out), .d(not_1_out), .c(not_4_out),
    .dp(not_8_out));
  not not_5 (not_5_out, P1_4);
  not not_6 (not_6_out, P1_5);
  not not_7 (not_7_out, P1_6);
  not not_8 (not_8_out, P1_7);

  // Notes on the sheet:
  //   a
  //   b
  //   c
  //   d
  //   e
  //   f
  //   g
  //   pd
endmodule
